# Fritzing sketch Dual 8-Bit Binary Counters (saved by Fritzing 0.9.2b)
breadboards: 1

parts:
  R3 = Resistor [tolerance=±5% resistance=220 package="2512 [SMD]"]
  LED8 = smd LED [color="Green (555nm)" package="0603 [SMD]"]
  R8 = Resistor [tolerance=±5% resistance=220 package="2512 [SMD]"]
  LED1 = smd LED [color="Green (555nm)" package="0603 [SMD]"]
  LED4 = smd LED [color="Green (555nm)" package="0603 [SMD]"]
  R4 = Resistor [tolerance=±5% resistance=220 package="2512 [SMD]"]
  Arduino_Board3 = Arduino Uno (Rev3) - ICSP
  LED5 = smd LED [color="Green (555nm)" package="0603 [SMD]"]
  R7 = Resistor [tolerance=±5% resistance=220 package="2512 [SMD]"]
  LED3 = smd LED [color="Green (555nm)" package="0603 [SMD]"]
  R1 = Resistor [tolerance=±5% resistance=220 package="2512 [SMD]"]
  R2 = Resistor [tolerance=±5% resistance=220 package="2512 [SMD]"]
  LED2 = smd LED [color="Green (555nm)" package="0603 [SMD]"]
  LED7 = smd LED [color="Green (555nm)" package="0603 [SMD]"]
  R6 = Resistor [tolerance=±5% resistance=220 package="2512 [SMD]"]
  IC2 = SHIFT REGISTER [package=dil16]
  LED6 = smd LED [color="Green (555nm)" package="0603 [SMD]"]
  R5 = Resistor [tolerance=±5% resistance=220 package="2512 [SMD]"]
  LED16 = smd LED [color="Red (633nm)" package="0805 [SMD]"]
  LED10 = smd LED [color="Red (633nm)" package="0805 [SMD]"]
  LED11 = smd LED [color="Red (633nm)" package="0805 [SMD]"]
  LED12 = smd LED [color="Red (633nm)" package="0805 [SMD]"]
  LED13 = smd LED [color="Red (633nm)" package="0805 [SMD]"]
  LED14 = smd LED [color="Red (633nm)" package="0805 [SMD]"]
  LED15 = smd LED [color="Red (633nm)" package="0805 [SMD]"]
  LED9 = smd LED [color="Red (633nm)" package="0805 [SMD]"]
  IC4 = SHIFT REGISTER [package=dil16]
  R9 = Resistor [tolerance=±5% resistance=220 package="2512 [SMD]"]
  R11 = Resistor [tolerance=±5% resistance=220 package="2512 [SMD]"]
  R12 = Resistor [tolerance=±5% resistance=220 package="2512 [SMD]"]
  R14 = Resistor [tolerance=±5% resistance=220 package="2512 [SMD]"]
  R13 = Resistor [tolerance=±5% resistance=220 package="2512 [SMD]"]
  R15 = Resistor [tolerance=±5% resistance=220 package="2512 [SMD]"]
  R16 = Resistor [tolerance=±5% resistance=220 package="2512 [SMD]"]
  R10 = Resistor [tolerance=±5% resistance=220 package="2512 [SMD]"]

nets:
  GND: R3.Pin_0, R8.Pin_0, R4.Pin_0, Arduino_Board3.GND, R7.Pin_0, R1.Pin_0, R2.Pin_0, R6.Pin_0, IC2.GND, IC2.G, R5.Pin_0, IC4.GND, IC4.SER, R9.Pin_0, R11.Pin_0, R12.Pin_0, R14.Pin_0, R13.Pin_0, R15.Pin_0, R16.Pin_0, R10.Pin_0
  N1: R3.Pin_1, LED2.cathode
  N2: LED8.cathode, R2.Pin_1
  N3: LED8.anode, IC2.QG
  N4: R8.Pin_1, LED6.cathode
  N5: LED1.cathode, R1.Pin_1
  N6: LED1.anode, IC2.QH
  N7: LED4.cathode, R5.Pin_1
  N8: LED4.anode, IC2.QC
  N9: R4.Pin_1, LED3.cathode
  N10: Arduino_Board3.D8, IC2.RCK, IC4.G
  N11: Arduino_Board3.D11_PWM/MOSI, IC2.SER
  N12: Arduino_Board3.D12/MISO, IC2.SCK, IC4.RCK
  VCC: Arduino_Board3.3V3, IC2.SCL, IC2.VCC, LED16.anode, IC4.QA, IC4.VCC
  N13: LED5.cathode, R7.Pin_1
  N14: LED5.anode, IC2.QB
  N15: LED3.anode, IC2.QE
  N16: LED2.anode, IC2.QF
  N17: LED7.cathode, R6.Pin_1
  N18: LED7.anode, IC2.QD
  N19: IC2.QA, LED6.anode
  N20: LED16.cathode, R16.Pin_1
  N21: LED10.cathode, R10.Pin_1
  N22: LED10.anode, IC4.QG
  N23: LED11.cathode, R11.Pin_1
  N24: LED11.anode, IC4.QF
  N25: LED12.cathode, R12.Pin_1
  N26: LED12.anode, IC4.QE
  N27: LED13.cathode, R13.Pin_1
  N28: LED13.anode, IC4.QD
  N29: LED14.cathode, R14.Pin_1
  N30: LED14.anode, IC4.QC
  N31: LED15.cathode, R15.Pin_1
  N32: LED15.anode, IC4.QB
  N33: LED9.cathode, R9.Pin_1
  N34: LED9.anode, IC4.QH
