# Fritzing sketch Interactive Traffic Lights (saved by Fritzing 0.9.2b)
breadboards: 1

parts:
  Part2 = Arduino Uno (Rev3) - ICSP
  LED2 = LED - 3mm [color="Yellow (592nm)" package="3 mm [THT]"]
  LED3 = LED - 3mm [color="Green (570nm)" package="3 mm [THT]"]
  LED4 = LED - 3mm [color="Green (570nm)" package="3 mm [THT]"]
  LED5 = LED - 3mm [color="Red (633nm)" package="3 mm [THT]"]
  LED1 = LED - 3mm [color="Red (633nm)" package="3 mm [THT]"]
  S2 = Pushbutton [package="[THT]"]
  R2 = Resistor [tolerance=±5% resistance=220 package="0805 [SMD]"]
  R3 = Resistor [tolerance=±5% resistance=220 package="0805 [SMD]"]
  R1 = Resistor [tolerance=±5% resistance=220 package="0805 [SMD]"]
  R4 = Resistor [tolerance=±5% resistance=220 package="0805 [SMD]"]
  R5 = Resistor [tolerance=±5% resistance=220 package="0805 [SMD]"]
  R6 = Resistor [tolerance=±5% resistance=220 package="0805 [SMD]"]

nets:
  N1: Part2.5V, S2.Pin_1, S2.Pin_2
  N2: Part2.ICSP_MOSI, Part2.D11_PWM/MOSI, R2.Pin_1
  N3: Part2.GND, LED2.cathode, LED3.cathode, LED4.cathode, LED5.cathode, LED1.cathode, R6.Pin_0
  N4: Part2.D8, R5.Pin_1
  N5: Part2.D9_PWM, R4.Pin_1
  N6: Part2.D10_PWM/SS, R3.Pin_1
  N7: Part2.D12/MISO, R1.Pin_1
  N8: Part2.D2, S2.Pin_3, S2.Pin_4, R6.Pin_1
  N9: LED2.anode, R2.Pin_0
  N10: LED3.anode, R3.Pin_0
  N11: LED4.anode, R4.Pin_0
  N12: LED5.anode, R5.Pin_0
  N13: LED1.anode, R1.Pin_0
