# Fritzing sketch Shift Register 8-Bit Binary Counter (saved by Fritzing 0.9.2b)
breadboards: 1

parts:
  R3 = Resistor [tolerance=±5% resistance=220 package="2512 [SMD]"]
  LED8 = smd LED [color="Green (555nm)" package="0603 [SMD]"]
  R8 = Resistor [tolerance=±5% resistance=220 package="2512 [SMD]"]
  LED1 = smd LED [color="Green (555nm)" package="0603 [SMD]"]
  LED5 = smd LED [color="Green (555nm)" package="0603 [SMD]"]
  R4 = Resistor [tolerance=±5% resistance=220 package="2512 [SMD]"]
  Arduino_Board3 = Arduino Uno (Rev3) - ICSP
  LED6 = smd LED [color="Green (555nm)" package="0603 [SMD]"]
  R7 = Resistor [tolerance=±5% resistance=220 package="2512 [SMD]"]
  LED3 = smd LED [color="Green (555nm)" package="0603 [SMD]"]
  R1 = Resistor [tolerance=±5% resistance=220 package="2512 [SMD]"]
  R2 = Resistor [tolerance=±5% resistance=220 package="2512 [SMD]"]
  LED2 = smd LED [color="Green (555nm)" package="0603 [SMD]"]
  LED4 = smd LED [color="Green (555nm)" package="0603 [SMD]"]
  R6 = Resistor [tolerance=±5% resistance=220 package="2512 [SMD]"]
  IC2 = SHIFT REGISTER [package=dil16]
  LED7 = smd LED [color="Green (555nm)" package="0603 [SMD]"]
  R5 = Resistor [tolerance=±5% resistance=220 package="2512 [SMD]"]

nets:
  GND: R3.Pin_0, R8.Pin_0, R4.Pin_0, Arduino_Board3.GND, R7.Pin_0, R1.Pin_0, R2.Pin_0, R6.Pin_0, IC2.GND, IC2.G, R5.Pin_0
  N1: R3.Pin_1, LED2.cathode
  N2: LED8.cathode, R2.Pin_1
  N3: LED8.anode, IC2.QG
  N4: R8.Pin_1, LED7.cathode
  N5: LED1.cathode, R1.Pin_1
  N6: LED1.anode, IC2.QH
  N7: LED5.cathode, R5.Pin_1
  N8: LED5.anode, IC2.QC
  N9: R4.Pin_1, LED3.cathode
  N10: Arduino_Board3.D8, IC2.RCK
  N11: Arduino_Board3.D11_PWM/MOSI, IC2.SER
  N12: Arduino_Board3.D12/MISO, IC2.SCK
  3V3: Arduino_Board3.3V3, IC2.SCL, IC2.VCC
  N13: LED6.cathode, R7.Pin_1
  N14: LED6.anode, IC2.QB
  N15: LED3.anode, IC2.QE
  N16: LED2.anode, IC2.QF
  N17: LED4.cathode, R6.Pin_1
  N18: LED4.anode, IC2.QD
  N19: IC2.QA, LED7.anode
