# Fritzing sketch Traffic Lights (saved by Fritzing 0.9.2b)
breadboards: 1

parts:
  LED3 = smd LED [color="Green (555nm)" package="0603 [SMD]"]
  LED2 = smd LED [color="Yellow (585nm)" package="0603 [SMD]"]
  LED1 = smd LED [color="Red (633nm)" package="0603 [SMD]"]
  R3 = Resistor [tolerance=±5% resistance=220 package="2512 [SMD]"]
  R2 = Resistor [tolerance=±5% resistance=220 package="2512 [SMD]"]
  R1 = Resistor [tolerance=±5% resistance=220 package="2512 [SMD]"]
  Arduino_Board2 = Arduino Uno (Rev3) - ICSP

nets:
  N1: LED3.cathode, LED2.cathode, LED1.cathode, Arduino_Board2.GND
  N2: LED3.anode, R3.Pin_1
  N3: LED2.anode, R2.Pin_1
  N4: LED1.anode, R1.Pin_1
  N5: R3.Pin_0, Arduino_Board2.D8
  N6: R2.Pin_0, Arduino_Board2.D9_PWM
  N7: R1.Pin_0, Arduino_Board2.D10_PWM/SS
